# Fritzing sketch Cable Notations (saved by Fritzing 0.9.4)
breadboards: 1

parts:
  U1 = ESP32S-HiLetgo [part_number=ESP32S-HiLetgo]
  R1 = Resistor [tolerance=±5% resistance=220 package=THT]
  LED1 = LED - 5mm [color="Red (633nm)" package="5 mm [THT]"]
  LED2 = LED - 5mm [color="Blue (430nm)" package="5 mm [THT]"]
  R3 = Resistor [tolerance=±5% resistance=220 package=THT]
  R4 = Resistor [tolerance=±5% resistance=220 package=THT]
  LED3 = LED - 5mm [color="Green (565nm)" package="5 mm [THT]"]
  R5 = Resistor [tolerance=±5% resistance=220 package=THT]
  R6 = Photocell (LDR) [package=THT]

nets:
  N1: U1.GPIO34, R5.Pin_1, R6.pin_0
  N2: U1.GPIO32, R4.Pin_1
  N3: U1.GPIO27, R3.Pin_1
  N4: U1.GPIO14, R1.Pin_1
  N5: U1.GND, LED1.cathode, LED2.cathode, LED3.cathode, R5.Pin_0
  N6: U1.VIN, R6.pin_1
  N7: R1.Pin_0, LED1.anode
  N8: LED2.anode, R4.Pin_0
  N9: R3.Pin_0, LED3.anode

custom parts:
  ESP32S-HiLetgo: HiLetgo ESP-WROOM-32 ESP32 ESP-32S Development Board 2.4GHz Dual-Mode WiFi + Bluetooth Dual Cores Microcontroller The ESP32 integrated with Antenna switches, RF Balun, power amplifiers, low-noise amplifiers, filters, and management modules, and the entire solution occupies the least area of PCB. 2.4 GHz Wi-Fi plus Bluetooth dual-mode chip, with TSMC Ultra-low power consumption 40nm technology,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
